# Fritzing sketch 20200227_circuit_kit (saved by Fritzing 0.9.4)
breadboards: 1

parts:
  U1 = BNC [package=bnc]
  C1 = Ceramic Capacitor [capacitance=1µF voltage=16V package="100 mil [THT, multilayer]"]
  R1 = Resistor [tolerance=±5% resistance=1k package=THT]

nets:
  GND: U1.GND, R1.Pin_0
  N1: U1.OUT, C1.0, R1.Pin_1
  P0[5]: C1.1

notes:
  INPUT
